# Fritzing sketch Mouser_LightedWaterCan_1V0 (saved by Fritzing 0.9.3b)

parts:
  Part1 = Adafruit Feather M0 Bluefruit LE [part_number="Adafruit #2995"]
  JACK1 = 2.1mm DC Barrel Jack
  LED1 = LEDs [package=led10mm]

nets:
  N1: Part1.GND, JACK1.switch, LED1.C
  N2: Part1.VBUS, JACK1.center
  N3: Part1.D9, LED1.A

custom parts:
  Adafruit Feather M0 Bluefruit LE: This is the Adafruit Feather M0 Bluefruit LE - our take on an 'all-in-one' Arduino-compatible + Bluetooth Low Energy with built in USB and battery charging. Its an Adafruit Feather M0 with a BTLE module, ready to rock! We have other boards in the Feather family, check'em out here. Bluetooth Low Energy is the hottest new low-power, 2.4GHz spectrum wireless protocol. In particular, its the only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
  2.1mm DC Barrel Jack: 2.1mm DC Barrel Jack with Thru-Hole Connectors (breadboardable)
